# Fritzing sketch Invernadero (saved by Fritzing 0.8.5b)
breadboards: 1

parts:
  Parte1 = Arduino Yun
  KY-1 = Keyes Relay [package=THT]
  KY-2 = Keyes Relay [package=THT]
  KY-3 = Keyes Relay [package=THT]
  KY-4 = Keyes Relay [package=THT]
  PIR1 = PIR sensor
  Parte2 = HC-SR04
  RHT1 = Humidity and Temperature Sensor RHT03
  R2 = Photocell (LDR) [package=THT]
  R3 = Resistor [tolerance=±5% resistance=1k package=THT]

nets:
  N1: Parte1.A0, R2.pin_0, R3.Pin_0
  N2: Parte1.D8, RHT1.Data-signal
  N3: Parte1.D9_PWM, PIR1.SIG
  N4: Parte1.D2, Parte2.Echo
  N5: Parte1.D3_PWM, Parte2.Trig
  N6: Parte1.D4, KY-1.signal
  N7: Parte1.D5_PWM, KY-2.signal
  N8: Parte1.D6_PWM, KY-3.signal
  N9: Parte1.D7, KY-4.signal
  VCC: Parte1.5V, KY-1.power, KY-2.power, KY-3.power, KY-4.power, PIR1.VDD, Parte2.Vcc, RHT1.Vcc, R3.Pin_1
  GND: Parte1.GND, KY-1.ground, KY-2.ground, KY-3.ground, KY-4.ground, PIR1.GND, Parte2.Gnd, RHT1.GND_2, R2.pin_1

custom parts:
  Arduino Yun: The new Arduino Yun is a microcontroller board based on the ATmega32u4 (datasheet) and the Atheros AR9331. The Atheros processor supports a Linux distribution based on OpenWRT named Linino. The board has built-in Ethernet and WiFi support, a USB-A port, micro-SD card slot, 20 digital input/output pins (of which 7 can be used as PWM outputs and 12 as analog inputs), a 16 MHz crystal oscillator,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
  Keyes Relay: The Keyes 5V relay module is suitable for SCM development, home appliance control. It uses a 5V~12V TIL control signal which can control DC / AC signal.
  HC-SR04: HC-SR04 ultrasonic distance sensor
